// Logisim project COA241210059.circ as structural Verilog: 1 circuit, main circuit main
module main (
  input  in_1,
  input  [2:0] in_2,
  input  in_3,
  input  in_4,
  input  in_5,
  input  in_6,
  input  in_7,
  input  in_8,
  input  in_9,
  input  in_10,
  input  in_11,
  input  in_12,
  input  in_13,
  input  in_14,
  input  in_15,
  input  in_16,
  input  in_17,
  input  in_18,
  input  in_19,
  input  in_20,
  input  in_21,
  input  in_22,
  output out_23,
  output out_24,
  output out_25,
  output out_26,
  output out_27
);

  wire multiplexer_1_out, multiplexer_2_out, multiplexer_3_out, multiplexer_4_out, multiplexer_5_out,
       multiplexer_6_out;
  wire [2:0] priority_encoder_1_out;

  Multiplexer multiplexer_1 (.in0(in_1), .in1(in_3), .out(multiplexer_1_out), .sel(in_4));
  Multiplexer multiplexer_2 (.in0(in_5), .in1(in_7), .out(multiplexer_2_out), .sel(in_8));
  Multiplexer multiplexer_3 (.in0(in_16), .in1(in_17), .out(multiplexer_3_out), .sel(in_18));
  Multiplexer multiplexer_4 (.in0(in_20), .in1(in_21), .out(multiplexer_4_out), .sel(in_22));
  Multiplexer multiplexer_5 (.in0(multiplexer_1_out), .in1(multiplexer_2_out), .out(multiplexer_5_out), .sel(in_6));
  Multiplexer multiplexer_6 (.in0(multiplexer_3_out), .in1(multiplexer_4_out), .out(multiplexer_6_out), .sel(in_19));
  Multiplexer #(.select(3)) multiplexer_7 (
    .in0(1'b1), .in1(1'b1), .in2(1'b1), .in3(1'b1), .in4(1'b0), .in5(1'b0), .in6(1'b1), .in7(1'b1),
    .out(out_23), .sel(in_2));
  Multiplexer multiplexer_8 (.in0(multiplexer_5_out), .in1(multiplexer_6_out), .out(out_24));  // open: sel
  Priority_Encoder priority_encoder_1 (
    .in0(1'b1), .in1(1'b1), .in2(1'b1), .in3(1'b0), .in4(1'b1), .in5(1'b1), .in6(1'b1), .in7(1'b1),
    .out(priority_encoder_1_out));  // open: en_in, gs, en_out
  or or_1 (out_25, in_15, in_14, in_13, in_12);
  or or_2 (out_26, in_15, in_14, in_11, in_10);
  or or_3 (out_27, in_15, in_11, in_13, in_9);
  // also tied to VCC on the sheet: {priority_encoder_1_out[0], priority_encoder_1_out[1], priority_encoder_1_out[2]}

  // Notes on the sheet:
  //   in_13: initial=0x1
  //   in_14: initial=0x1
  //   in_15: initial=0x1
  //   in_1: initial=0x1
  //   in_9: initial=0x1
endmodule
