// Logisim project logical_shift_operations.circ as structural Verilog: 1 circuit, main circuit main
module main (
  input  in_1,
  input  in_2,
  input  in_3,
  input  in_4,
  input  in_5,
  input  in_6,
  input  in_7,
  output out_8,
  output out_9,
  output out_10,
  output out_11,
  output out_12,
  output out_13,
  output out_14,
  output out_15,
  output out_16,
  output out_17,
  output out_18,
  output out_19,
  output out_20,
  output out_21,
  output out_22,
  output out_23,
  output out_24,
  output out_25,
  output out_26,
  output out_27,
  output out_28,
  output out_29,
  output out_30,
  output out_31,
  output out_32,
  output out_33,
  output out_34,
  output out_35,
  output out_36,
  output out_37,
  output out_38,
  output out_39,
  output out_40,
  output out_41,
  output out_42,
  output out_43,
  output out_44,
  output out_45,
  output out_46,
  output out_47,
  output out_48,
  output out_49
);

  wire clock_1_out, clock_2_out, clock_3_out, clock_4_out, clock_5_out, clock_6_out;

  D_Flip_Flop d_ff_1 (.D(out_14), .clk(clock_1_out), .Q(out_10));  // open: Qn, preset, reset
  D_Flip_Flop d_ff_2 (.D(out_18), .clk(clock_1_out), .Q(out_14));  // open: Qn, preset, reset
  D_Flip_Flop d_ff_3 (.D(out_22), .clk(clock_1_out), .Q(out_18));  // open: Qn, preset, reset
  Clock clock_1 (.out(clock_1_out));
  Clock clock_2 (.out(clock_2_out));
  D_Flip_Flop d_ff_4 (.D(out_26), .clk(clock_1_out), .Q(out_22));  // open: Qn, preset, reset
  D_Flip_Flop d_ff_5 (.D(out_30), .clk(clock_1_out), .Q(out_26));  // open: Qn, preset, reset
  D_Flip_Flop d_ff_6 (.D(out_34), .clk(clock_1_out), .Q(out_30));  // open: Qn, preset, reset
  D_Flip_Flop d_ff_7 (.D(in_5), .clk(clock_1_out), .Q(out_34));  // open: Qn, preset, reset
  D_Flip_Flop d_ff_8 (.D(out_38), .clk(clock_2_out), .Q(out_36));  // open: Qn, preset, reset
  D_Flip_Flop d_ff_9 (.D(out_40), .clk(clock_2_out), .Q(out_38));  // open: Qn, preset, reset
  D_Flip_Flop d_ff_10 (.D(out_42), .clk(clock_2_out), .Q(out_40));  // open: Qn, preset, reset
  D_Flip_Flop d_ff_11 (.D(out_44), .clk(clock_2_out), .Q(out_42));  // open: Qn, preset, reset
  D_Flip_Flop d_ff_12 (.D(out_46), .clk(clock_2_out), .Q(out_44));  // open: Qn, preset, reset
  D_Flip_Flop d_ff_13 (.D(out_48), .clk(clock_2_out), .Q(out_46));  // open: Qn, preset, reset
  D_Flip_Flop d_ff_14 (.D(in_7), .clk(clock_2_out), .Q(out_48));  // open: Qn, preset, reset
  Clock clock_3 (.out(clock_3_out));
  Clock clock_4 (.out(clock_4_out));
  D_Flip_Flop d_ff_15 (.D(in_6), .clk(clock_3_out), .Q(out_37));  // open: Qn, preset, reset
  D_Flip_Flop d_ff_16 (.D(out_37), .clk(clock_3_out), .Q(out_39));  // open: Qn, preset, reset
  D_Flip_Flop d_ff_17 (.D(out_39), .clk(clock_3_out), .Q(out_41));  // open: Qn, preset, reset
  D_Flip_Flop d_ff_18 (.D(out_41), .clk(clock_3_out), .Q(out_43));  // open: Qn, preset, reset
  D_Flip_Flop d_ff_19 (.D(out_43), .clk(clock_3_out), .Q(out_45));  // open: Qn, preset, reset
  D_Flip_Flop d_ff_20 (.D(out_45), .clk(clock_3_out), .Q(out_47));  // open: Qn, preset, reset
  D_Flip_Flop d_ff_21 (.D(out_47), .clk(clock_3_out), .Q(out_49));  // open: Qn, preset, reset
  D_Flip_Flop d_ff_22 (.D(in_2), .clk(clock_4_out), .Q(out_11));  // open: Qn, preset, reset
  D_Flip_Flop d_ff_23 (.D(out_11), .clk(clock_4_out), .Q(out_15));  // open: Qn, preset, reset
  D_Flip_Flop d_ff_24 (.D(out_15), .clk(clock_4_out), .Q(out_19));  // open: Qn, preset, reset
  D_Flip_Flop d_ff_25 (.D(out_19), .clk(clock_4_out), .Q(out_23));  // open: Qn, preset, reset
  D_Flip_Flop d_ff_26 (.D(out_23), .clk(clock_4_out), .Q(out_27));  // open: Qn, preset, reset
  D_Flip_Flop d_ff_27 (.D(out_27), .clk(clock_4_out), .Q(out_31));  // open: Qn, preset, reset
  D_Flip_Flop d_ff_28 (.D(out_31), .clk(clock_4_out), .Q(out_35));  // open: Qn, preset, reset
  Clock clock_5 (.out(clock_5_out));
  D_Flip_Flop d_ff_29 (.D(in_1), .clk(clock_5_out), .Q(out_8));  // open: Qn, preset, reset
  D_Flip_Flop d_ff_30 (.D(out_8), .clk(clock_5_out), .Q(out_12));  // open: Qn, preset, reset
  D_Flip_Flop d_ff_31 (.D(out_12), .clk(clock_5_out), .Q(out_16));  // open: Qn, preset, reset
  D_Flip_Flop d_ff_32 (.D(out_16), .clk(clock_5_out), .Q(out_20));  // open: Qn, preset, reset
  D_Flip_Flop d_ff_33 (.D(out_20), .clk(clock_5_out), .Q(out_24));  // open: Qn, preset, reset
  D_Flip_Flop d_ff_34 (.D(out_24), .clk(clock_5_out), .Q(out_28));  // open: Qn, preset, reset
  D_Flip_Flop d_ff_35 (.D(out_28), .clk(clock_5_out), .Q(out_32));  // open: Qn, preset, reset
  D_Flip_Flop d_ff_36 (.D(out_13), .clk(clock_6_out), .Q(out_9));  // open: Qn, preset, reset
  D_Flip_Flop d_ff_37 (.D(out_17), .clk(clock_6_out), .Q(out_13));  // open: Qn, preset, reset
  D_Flip_Flop d_ff_38 (.D(out_21), .clk(clock_6_out), .Q(out_17));  // open: Qn, preset, reset
  D_Flip_Flop d_ff_39 (.D(out_25), .clk(clock_6_out), .Q(out_21));  // open: Qn, preset, reset
  D_Flip_Flop d_ff_40 (.D(out_29), .clk(clock_6_out), .Q(out_25));  // open: Qn, preset, reset
  D_Flip_Flop d_ff_41 (.D(in_3), .clk(clock_6_out), .Q(out_29));  // open: Qn, preset, reset
  D_Flip_Flop d_ff_42 (.D(in_4), .clk(clock_6_out), .Q(out_33));  // open: Qn, preset, reset
  Clock clock_6 (.out(clock_6_out));
endmodule
